// Logisim project 1A.circ as structural Verilog: 1 circuit, main circuit main
module main (
  input  in_1,
  input  in_2,
  input  in_3,
  input  A,
  input  B,
  input  in_6,
  input  in_7,
  input  in_8,
  input  in_9,
  input  in_10,
  input  in_11,
  input  in_12,
  input  in_13,
  input  in_14,
  input  in_15,
  input  in_16,
  input  in_17,
  input  in_18,
  input  in_19,
  input  in_20,
  output out_21,
  output Y_A_B,
  output out_23,
  output out_24,
  output out_25,
  output out_26,
  output out_27,
  output out_28,
  output out_29
);

  and and_1 (Y_A_B, A, B);
  or or_1 (out_24, in_9, in_10);
  not not_1 (out_26, in_13);
  xor xor_1 (out_28, in_15, in_17);
  and and_2 (out_29, in_18, in_19, in_20);
  nand nand_1 (out_21, in_1, in_2, in_3);
  NotExactlyOne xnor_1 (.out(out_23), .in0(in_6), .in1(in_7), .in2(in_8));
  nand nand_2 (out_25, in_11, in_12);
  nor nor_1 (out_27, in_14, in_16);
endmodule
