// Logisim project 2b.circ as structural Verilog: 1 circuit, main circuit main
module main (
  input  D,
  input  C,
  input  B,
  input  A,
  output Z,
  output Y,
  output X,
  output W
);

  wire and_1_out, and_2_out, and_3_out, and_4_out, not_1_out, not_3_out, or_1_out;

  not not_1 (not_1_out, B);
  not not_2 (Z, D);
  buf and_1 (and_1_out, C);  // AND_Gate
  or or_1 (or_1_out, D, C);
  not not_3 (not_3_out, or_1_out);
  buf or_2 (Y, and_1_out);  // OR_Gate
  and and_2 (and_2_out, not_3_out, B);
  and and_3 (and_3_out, or_1_out, not_1_out);
  and and_4 (and_4_out, or_1_out, B);
  or or_3 (X, and_2_out, and_3_out);
  or or_4 (W, and_4_out, A);
endmodule
