// Logisim project 2ba.circ as structural Verilog: 1 circuit, main circuit main
module main (
  input  in_1,
  input  in_2,
  input  in_3,
  input  in_4,
  input  in_5,
  input  in_6,
  input  in_7,
  input  in_8,
  input  in_9,
  output out_10,
  output out_11,
  output out_12,
  output out_13
);

  wire buffer_1_out, not_1_out, or_1_out, or_2_out, or_3_out;

  not not_1 (not_1_out, in_6);
  or or_1 (or_1_out, in_1, in_2);
  buf or_2 (or_2_out, in_4);  // OR_Gate
  buf or_3 (or_3_out, not_1_out);  // OR_Gate
  and and_1 (out_10, or_1_out, in_3);
  and and_2 (out_11, or_2_out, or_2_out, in_5);
  and and_3 (out_12, or_3_out, in_7);
  buf buffer_1 (buffer_1_out, in_8);
  or or_4 (out_13, buffer_1_out, in_9);
endmodule
