// Logisim project 2bb.circ as structural Verilog: 1 circuit, main circuit main
module main (
  input  in_1,
  input  in_2,
  input  in_3,
  input  in_4,
  input  in_5,
  input  in_6,
  input  in_7,
  input  in_8,
  input  in_9,
  input  in_10,
  input  in_11,
  input  in_12,
  input  in_13,
  input  in_14,
  input  in_15,
  input  in_16,
  input  in_17,
  input  in_18,
  output out_19,
  output out_20,
  output out_21,
  output out_22,
  output out_23,
  output out_24
);

  wire and_2_out, and_4_out, and_5_out, not_1_out, or_3_out, or_4_out;

  and and_1 (out_19, in_1, in_3);
  or or_1 (out_21, in_5, in_6, in_7);
  and and_2 (and_2_out, in_10, in_12);
  or or_2 (out_23, and_2_out, in_14);
  or or_3 (or_3_out, in_15, in_16);
  or or_4 (or_4_out, in_17, in_18);
  not not_1 (not_1_out, in_2);
  and and_3 (out_24, or_3_out, or_4_out);
  not not_2 (out_20, in_4);
  and and_4 (and_4_out, in_8, in_9);
  and and_5 (and_5_out, in_11, in_13);
  or or_5 (out_22, and_4_out, and_5_out);
endmodule
