// Logisim project 2exp.circ as structural Verilog: 1 circuit, main circuit main
module main (
  input  in_1,
  input  in_2,
  input  in_3,
  input  in_4,
  input  in_5,
  input  in_6,
  input  in_7,
  input  in_8,
  input  in_9,
  input  in_10,
  input  in_11,
  output out_12,
  output out_13,
  output out_14,
  output out_15,
  output out_16,
  output out_17,
  output out_18
);

  wire and_1_out, and_3_out, and_5_out, not_1_out, or_1_out, xor_1_out;

  and and_1 (and_1_out, in_6, in_7);
  xor xor_1 (xor_1_out, in_1, in_2);
  or or_1 (or_1_out, in_5, and_1_out);
  xor xor_2 (out_16, in_9, in_11);
  and and_2 (out_18, in_9, in_11);
  and and_3 (and_3_out, in_1, in_2);
  and and_4 (out_14, in_4, or_1_out);
  xor xor_3 (out_12, xor_1_out, in_3);
  and and_5 (and_5_out, xor_1_out, in_3);
  or or_2 (out_13, and_5_out, and_3_out);
  not not_1 (not_1_out, in_8);
  xor xor_4 (out_15, in_8, in_10);
  and and_6 (out_17, not_1_out, not_1_out, in_10);
endmodule
