// Logisim project 4asubtrator.circ as structural Verilog: 2 circuits, main circuit full subtrator
module full_subtrator (
  input  in_1,
  input  in_2,
  input  in_3,
  output out_4,
  output out_5
);

  wire and_1_out, and_2_out, and_3_out, not_1_out, or_1_out, xor_1_out;

  not not_1 (not_1_out, in_1);
  xor xor_1 (xor_1_out, in_1, in_2);
  and and_1 (and_1_out, not_1_out, in_2);
  and and_2 (and_2_out, in_2, in_3);
  and and_3 (and_3_out, in_2, in_3);
  or or_1 (or_1_out, and_1_out, and_2_out);
  xor xor_2 (out_4, xor_1_out, in_3);
  or or_2 (out_5, or_1_out, and_3_out);
endmodule

module _4bit_subtrator (
  input  in_1,
  input  in_2,
  input  in_3,
  input  in_4,
  input  in_5,
  input  in_6,
  input  in_7,
  input  in_8,
  input  in_9,
  input  in_10,
  output out_11,
  output out_12,
  output out_13,
  output out_14,
  output out_15
);

  wire full_subtrator_2_out_5, full_subtrator_3_out_5, full_subtrator_4_out_5, xor_1_out, xor_2_out,
       xor_3_out, xor_4_out;

  xor xor_1 (xor_1_out, in_3, in_1);
  full_subtrator full_subtrator_1 (
    .in_1(full_subtrator_2_out_5), .in_2(xor_1_out), .in_3(in_2), .out_4(out_13), .out_5(out_12));
  xor xor_2 (xor_2_out, in_5, in_1);
  full_subtrator full_subtrator_2 (
    .in_1(full_subtrator_3_out_5), .in_2(xor_2_out), .in_3(in_4), .out_4(out_14),
    .out_5(full_subtrator_2_out_5));
  xor xor_3 (xor_3_out, in_7, in_1);
  full_subtrator full_subtrator_3 (
    .in_1(full_subtrator_4_out_5), .in_2(xor_3_out), .in_3(in_6), .out_4(out_15),
    .out_5(full_subtrator_3_out_5));
  xor xor_4 (xor_4_out, in_9, in_1);
  full_subtrator full_subtrator_4 (
    .in_1(in_10), .in_2(xor_4_out), .in_3(in_8), .out_4(out_11), .out_5(full_subtrator_4_out_5));
endmodule
