// Logisim project 4bbcdadder.circ as structural Verilog: 3 circuits, main circuit full adder
module full_adder (
  input  in_1,
  input  in_2,
  input  in_3,
  output out_4,
  output out_5
);

  wire and_1_out, and_2_out, xor_1_out;

  xor xor_1 (xor_1_out, in_1, in_2);
  and and_1 (and_1_out, in_1, in_2);
  xor xor_2 (out_4, xor_1_out, in_3);
  and and_2 (and_2_out, xor_1_out, in_3);
  or or_1 (out_5, and_2_out, and_1_out);
endmodule

module _4bit_adder (
  input  in_1,
  input  in_2,
  input  in_3,
  input  in_4,
  input  in_5,
  input  in_6,
  input  in_7,
  input  in_8,
  input  c_in,
  output c_out,
  output s4,
  output s2,
  output out_13,
  output s3
);

  wire full_adder_2_out_5, full_adder_3_out_5, full_adder_4_out_5;

  full_adder full_adder_1 (.in_1(full_adder_2_out_5), .in_2(in_2), .in_3(in_1), .out_4(s4), .out_5(c_out));
  full_adder full_adder_2 (.in_1(full_adder_3_out_5), .in_2(in_4), .in_3(in_3), .out_4(s3), .out_5(full_adder_2_out_5));
  full_adder full_adder_3 (.in_1(full_adder_4_out_5), .in_2(in_6), .in_3(in_5), .out_4(s2), .out_5(full_adder_3_out_5));
  full_adder full_adder_4 (.in_1(c_in), .in_2(in_8), .in_3(in_7), .out_4(out_13), .out_5(full_adder_4_out_5));

  // Notes on the sheet:
  //   s1
endmodule

module bcd_addrer (
  input  in_1,
  input  in_2,
  input  in_3,
  input  in_4,
  input  in_5,
  input  in_6,
  input  in_7,
  input  in_8,
  input  in_9,
  input  in_10,
  input  in_11,
  output out_12,
  output out_13,
  output out_14,
  output out_15,
  output out_16,
  output out_17
);

  wire and_1_out, and_2_out, full_adder_1_out_4, full_adder_3_out_4, full_adder_3_out_5, full_adder_4_out_5,
       full_adder_5_out_4, full_adder_5_out_5, full_adder_6_out_5, full_adder_7_out_4, full_adder_7_out_5,
       full_adder_8_out_5, or_1_out;

  or or_1 (or_1_out, and_1_out, out_12, and_2_out);
  full_adder full_adder_1 (
    .in_1(full_adder_3_out_5), .in_2(in_4), .in_3(in_3), .out_4(full_adder_1_out_4), .out_5(out_12));
  and and_1 (and_1_out, full_adder_1_out_4, full_adder_3_out_4);
  and and_2 (and_2_out, full_adder_5_out_4, full_adder_1_out_4);
  full_adder full_adder_2 (
    .in_1(full_adder_4_out_5), .in_2(full_adder_1_out_4), .in_3(in_11), .out_4(out_17), .out_5(out_16));
  full_adder full_adder_3 (
    .in_1(full_adder_5_out_5), .in_2(in_2), .in_3(in_1), .out_4(full_adder_3_out_4),
    .out_5(full_adder_3_out_5));
  full_adder full_adder_4 (
    .in_1(full_adder_6_out_5), .in_2(full_adder_3_out_4), .in_3(or_1_out), .out_4(out_14),
    .out_5(full_adder_4_out_5));
  full_adder full_adder_5 (
    .in_1(full_adder_7_out_5), .in_2(in_8), .in_3(in_7), .out_4(full_adder_5_out_4),
    .out_5(full_adder_5_out_5));
  full_adder full_adder_6 (
    .in_1(full_adder_8_out_5), .in_2(full_adder_5_out_4), .in_3(or_1_out), .out_4(out_15),
    .out_5(full_adder_6_out_5));
  full_adder full_adder_7 (
    .in_1(in_9), .in_2(in_6), .in_3(in_5), .out_4(full_adder_7_out_4), .out_5(full_adder_7_out_5));
  full_adder full_adder_8 (
    .in_1(in_10), .in_2(full_adder_7_out_4), .in_3(in_11), .out_4(out_13), .out_5(full_adder_8_out_5));
endmodule
