// Logisim project ex4c.circ as structural Verilog: 1 circuit, main circuit main
module main (
  input  in_1,
  input  in_2,
  input  in_3,
  input  Y1,
  input  Y2,
  input  Y3,
  input  Y4,
  input  Y5,
  input  Y6,
  input  Y7,
  output out_11,
  output out_12,
  output A2,
  output A1,
  output A0
);

  or or_1 (out_11, in_1, in_2);
  or or_2 (out_12, in_1, in_3);
  or or_3 (A2, Y7, Y6, Y5, Y4);
  or or_4 (A1, Y7, Y6, Y3, Y2);
  or or_5 (A0, Y7, Y5, Y3, Y1);
endmodule
