// Logisim project ex4d.circ as structural Verilog: 1 circuit, main circuit main
module main (
  input  A0,
  input  A1,
  input  in_3,
  input  in_4,
  input  in_5,
  input  E,
  output Y3,
  output Y2,
  output Y1,
  output Y0
);

  wire not_1_out, not_2_out, not_3_out, not_4_out, not_5_out;

  not not_1 (not_1_out, A0);
  not not_2 (not_2_out, A1);
  and and_1 (Y3, A0, A1, E);
  and and_2 (Y2, A0, not_2_out, E);
  and and_3 (Y1, not_1_out, A1, E);
  and and_4 (Y0, not_1_out, not_2_out, E);
  not not_3 (not_3_out, in_3);
  not not_4 (not_4_out, in_4);
  not not_5 (not_5_out, in_5);
  // AND_Gate and_5 has open pins: in2=not_3_out, in3=not_4_out, in4=not_5_out, out=open
  // AND_Gate and_6 has open pins: in0=in_3, in1=not_4_out, in3=not_5_out, out=open
  // AND_Gate and_7 has open pins: in0=not_3_out, in1=in_4, in2=not_5_out, out=open
  // AND_Gate and_8 has open pins: in1=in_4, in2=not_5_out, in3=in_3, out=open
  // AND_Gate and_9 is placed but not wired
  // AND_Gate and_10 has open pins: in1=in_5, in3=not_4_out, out=open
  // AND_Gate and_11 has open pins: in0=not_3_out, out=open
  // AND_Gate and_12 has open pins: in1=in_3, out=open
endmodule
