// Logisim project ex5.circ as structural Verilog: 1 circuit, main circuit main
module main (
  input  D0,
  input  D1,
  input  D2,
  input  D3,
  input  S0,
  input  in_6,
  output out_7
);

  wire and_1_out, and_2_out, and_3_out, and_4_out, not_1_out, not_2_out, or_1_out, or_2_out;

  not not_1 (not_1_out, in_6);
  not not_2 (not_2_out, S0);
  and and_1 (and_1_out, D0, not_2_out, not_1_out);
  and and_2 (and_2_out, not_2_out, D2, in_6);
  and and_3 (and_3_out, not_1_out, D1, not_2_out);
  and and_4 (and_4_out, D3, in_6, S0);
  or or_1 (or_1_out, and_1_out, and_3_out);
  or or_2 (or_2_out, and_2_out, and_4_out);
  or or_3 (out_7, or_1_out, or_1_out, or_2_out);

  // Notes on the sheet:
  //   S1
endmodule
