// Logisim project ex6.circ as structural Verilog: 1 circuit, main circuit main
module main (
  input  in_1
);

  wire and_1_out, and_2_out, clock_1_out, j_k_ff_1_q, j_k_ff_2_q, j_k_ff_3_q, j_k_ff_5_q;

  Clock clock_1 (.out(clock_1_out));
  J_K_Flip_Flop j_k_ff_1 (.J(in_1), .clk(clock_1_out), .K(in_1), .Q(j_k_ff_1_q));  // open: Qn, preset, en, reset
  LED led_1 (.in(j_k_ff_1_q));
  LED led_2 (.in(j_k_ff_2_q));
  J_K_Flip_Flop j_k_ff_2 (
    .J(j_k_ff_1_q), .clk(clock_1_out), .K(j_k_ff_1_q), .Q(j_k_ff_2_q));  // open: Qn, preset, en, reset
  and and_1 (and_1_out, j_k_ff_1_q, j_k_ff_2_q);
  LED led_3 (.in(j_k_ff_3_q));
  J_K_Flip_Flop j_k_ff_3 (
    .J(and_1_out), .clk(clock_1_out), .K(and_1_out), .Q(j_k_ff_3_q));  // open: Qn, preset, en, reset
  and and_2 (and_2_out, and_1_out, j_k_ff_3_q);
  J_K_Flip_Flop j_k_ff_4 ();  // open: J, clk, K, Q, Qn, preset, en, reset
  J_K_Flip_Flop j_k_ff_5 (
    .J(and_2_out), .clk(clock_1_out), .K(and_2_out), .Q(j_k_ff_5_q));  // open: Qn, preset, en, reset
  LED led_4 (.in(j_k_ff_5_q));
  J_K_Flip_Flop j_k_ff_6 ();  // open: J, clk, K, Q, Qn, preset, en, reset

  // Notes on the sheet:
  //   D3
  //   0
  //   0
  //   D2
  //   0
  //   0
  //   D1
  //   0
  //   1
  //   D0
  //   1
  //   0
endmodule
