// Logisim project ex7.circ as structural Verilog: 1 circuit, main circuit main
module main (
  input  shift_right,
  input  i4,
  input  i3,
  input  i2,
  input  i1,
  input  shift_left,
  input  [1:0] in_7,
  output out_8,
  output out_9,
  output out_10,
  output out_11
);

  wire button_1_out, clock_1_out, multiplexer_1_out, multiplexer_2_out, multiplexer_3_out, multiplexer_4_out;

  Multiplexer #(.select(2)) multiplexer_1 (
    .in0(out_8), .in1(shift_right), .in2(out_9), .in3(i4), .out(multiplexer_1_out), .sel(in_7));  // open: en
  Multiplexer #(.select(2)) multiplexer_2 (
    .in0(out_9), .in1(out_8), .in2(clock_1_out), .in3(i3), .out(multiplexer_2_out), .sel(in_7));  // open: en
  Multiplexer #(.select(2)) multiplexer_3 (
    .in0(clock_1_out), .in1(out_9), .in2(i2), .in3(clock_1_out), .out(multiplexer_3_out), .sel(in_7));  // open: en
  Multiplexer #(.select(2)) multiplexer_4 (
    .in0(clock_1_out), .in1(clock_1_out), .in2(i1), .in3(shift_left), .out(multiplexer_4_out), .sel(in_7));  // open: en
  Clock clock_1 (.out(clock_1_out));
  D_Flip_Flop d_ff_1 (
    .clk(clock_1_out), .D(multiplexer_1_out), .Q(out_8), .reset(button_1_out));  // open: Qn, preset, en
  D_Flip_Flop d_ff_2 (
    .clk(clock_1_out), .D(multiplexer_2_out), .Q(out_9), .reset(button_1_out));  // open: Qn, preset, en
  D_Flip_Flop d_ff_3 (
    .clk(clock_1_out), .D(multiplexer_3_out), .Q(out_10), .reset(button_1_out));  // open: Qn, preset, en
  D_Flip_Flop d_ff_4 (
    .clk(clock_1_out), .D(multiplexer_4_out), .Q(out_11), .reset(button_1_out));  // open: Qn, preset, en
  Button button_1 (.out(button_1_out));
endmodule
